// Logisim project CS2200_Proj2.circ as structural Verilog: 5 circuits, main circuit Main
module Main (
);

  wire alu_3_alu_zero, ALU_Src, and_1_out, Branch, CLK, Disable_Int, IE, Int, IntAck, IR_WE, JALR, LDADR,
       LdEnInt, Load, Load_B_W, Load_Enable, MAR_WE, MDR_WE, mem_1_int, Mem_to_Reg, not_1_out, PC_WE,
       Reg_Write_Enable, RTI, Store_B_W, Store_Enable, Store_PC;
  wire [1:0] ALU_OP, LS2b, Z;
  wire [4:0] _1_Reg_RD, multiplexer_2_out, multiplexer_3_out, multiplexer_4_out, multiplexer_5_out;
  wire [5:0] OPCODE;
  wire [7:0] Store_byte_0, Store_byte_1, Store_byte_2, Store_byte_3;
  wire [20:0] _21b_Reg_OFFSET;
  wire [23:0] _24b_address, Extended21b_Reg_OFFSET;
  wire [31:0] _32b_Address, alu_2_alu_out, Extended_Immediate_OFF, Load_Data, MDR_q, multiplexer_1_out,
       multiplexer_6_out, multiplexer_7_out, multiplexer_8_out, multiplexer_9_out, multiplexer_10_out,
       multiplexer_11_out, multiplexer_12_out, Next_PC, PC, PC_4, RT_value, shifter_1_out, Stored_PC,
       Zero_Extended_Immediate;
  wire [31:26] MAR_q;

  ALU alu_1 (.Src_1_Data(PC), .Src_2__Data(32'h4), .Op(2'b00), .ALU_out(PC_4));  // open: ALU_Zero
  Register #(.width(32)) u_PC (.D(Next_PC), .en(PC_WE), .Q(PC), .clk(CLK));  // open: clr
  Clock clock_1 (.out(CLK));
  Multiplexer #(.width(32), .disabled(0), .enable("false")) multiplexer_1 (
    .in0(PC), .in1(_32b_Address), .out(multiplexer_1_out), .sel(Load));
  Register #(.width(32)) MDR (.D(Load_Data), .en(MDR_WE), .Q(MDR_q), .clk(CLK));  // open: clr
  Control control_1 (
    .CLK(CLK), .OPCODE(OPCODE), .Branch_2bit(Z), .IE(IE), .INT(Int), .RTI(RTI), .Disable_Int(Disable_Int),
    .Store_PC(Store_PC), .IntAck(IntAck), .LdEnInt(LdEnInt), .Branch(Branch), .Load(Load), .PC_WE(PC_WE),
    .MAR_WE(MAR_WE), .MDR_WE(MDR_WE), .IR_WE(IR_WE), .ALUOP1(ALU_OP[1]), .ALUOP0(ALU_OP[0]),
    .ALUSrc1(ALU_Src), .LD_ADR(LDADR), .Mem_to_Reg(Mem_to_Reg), .Store_B_W(Store_B_W),
    .Reg_Write_Enable(Reg_Write_Enable), .Load_B_W(Load_B_W), .Load_Enable(Load_Enable),
    .Store_Enable(Store_Enable), .JALR(JALR));
  Register #(.width(32)) MAR (
    .D(multiplexer_1_out), .en(MAR_WE), .Q({MAR_q, _24b_address, LS2b}), .clk(CLK));  // open: clr
  Register #(.width(32)) Instr_Reg (
    .D(MDR_q), .en(IR_WE), .Q({OPCODE, _1_Reg_RD, _21b_Reg_OFFSET}), .clk(CLK));  // open: clr
  assign Extended_Immediate_OFF = {{16{_21b_Reg_OFFSET[15]}}, _21b_Reg_OFFSET[15:0]};  // Bit_Extender bit_extender_1
  assign Zero_Extended_Immediate = {{16{1'b0}}, _21b_Reg_OFFSET[15:0]};  // Bit_Extender bit_extender_2
  assign Extended21b_Reg_OFFSET = {{3{1'b0}}, _21b_Reg_OFFSET};  // Bit_Extender bit_extender_3
  Multiplexer #(.width(5), .disabled(0), .enable("false")) multiplexer_2 (
    .in0(_1_Reg_RD), .in1(5'b11110), .out(multiplexer_2_out), .sel(Store_PC));
  Multiplexer #(.width(5), .disabled(0), .enable("false")) multiplexer_3 (
    .in0(_21b_Reg_OFFSET[4:0]), .in1(_1_Reg_RD), .out(multiplexer_3_out), .sel(Store_Enable));
  Multiplexer #(.width(5), .disabled(0), .enable("false")) multiplexer_4 (
    .in0(multiplexer_3_out), .in1({5{1'b0}}), .out(multiplexer_4_out), .sel(JALR));
  Multiplexer #(.width(5), .disabled(0), .enable("false")) multiplexer_5 (
    .in0(_21b_Reg_OFFSET[20:16]), .in1(_21b_Reg_OFFSET[4:0]), .out(multiplexer_5_out), .sel(JALR));
  Register_file register_file_1 (
    .CLOCK(CLK), .Src_1_Select(multiplexer_5_out), .Write_Enable(Reg_Write_Enable),
    .Register_Write(multiplexer_2_out), .Write_Data(multiplexer_7_out), .Src_2_Select(multiplexer_4_out),
    .Source_1_Data(RT_value), .Source_2_Data({Store_byte_3, Store_byte_2, Store_byte_1, Store_byte_0}),
    .Stored_PC(Stored_PC));
  Multiplexer #(.width(32), .disabled(0), .enable("false")) multiplexer_6 (
    .in0({Store_byte_3, Store_byte_2, Store_byte_1, Store_byte_0}), .in1(Extended_Immediate_OFF),
    .out(multiplexer_6_out), .sel(ALU_Src));
  Multiplexer #(.width(32), .disabled(0), .enable("false")) multiplexer_7 (
    .in0(multiplexer_10_out), .in1(PC), .out(multiplexer_7_out), .sel(Store_PC));
  Shifter #(.width(32)) shifter_1 (.in(Extended_Immediate_OFF), .\dist (5'b00010), .out(shifter_1_out));
  Multiplexer #(.width(32), .disabled(0), .enable("false")) multiplexer_8 (
    .in0(RT_value), .in1(PC_4), .out(multiplexer_8_out), .sel(LDADR));
  Mem mem_1 (
    .LS_2b_of__address(LS2b), .Load_B_W(Load_B_W), .Load_Data(Load_Data), ._24b__address(_24b_address),
    .Store_Byte_3(Store_byte_3), .Store_Byte_1(Store_byte_1), .Store_Enable(Store_Enable),
    .Store_Byte_2(Store_byte_2), .Store_byte_word(Store_B_W), .Store_Byte_0(Store_byte_0), .INT(mem_1_int));
  ALU alu_2 (.Src_1_Data(PC_4), .Src_2__Data(shifter_1_out), .Op(2'b00), .ALU_out(alu_2_alu_out));  // open: ALU_Zero
  ALU alu_3 (
    .Src_1_Data(multiplexer_8_out), .Src_2__Data(multiplexer_6_out), .Op(ALU_OP), .ALU_out(_32b_Address),
    .ALU_Zero(alu_3_alu_zero));
  Register #(.width(1)) IntR (.D(1'b1), .en(mem_1_int), .Q(Int), .clk(not_1_out), .clr(IntAck));
  not not_1 (not_1_out, CLK);
  Multiplexer #(.width(32), .disabled(0), .enable("false")) multiplexer_9 (
    .in0(PC_4), .in1(alu_2_alu_out), .out(multiplexer_9_out), .sel(and_1_out));
  and and_1 (and_1_out, Branch, alu_3_alu_zero);
  Multiplexer #(.width(32), .disabled(0), .enable("false")) multiplexer_10 (
    .in0(_32b_Address), .in1(Load_Data), .out(multiplexer_10_out), .sel(Mem_to_Reg));
  Multiplexer #(.width(32), .disabled(0), .enable("false")) multiplexer_11 (
    .in0(multiplexer_9_out), .in1(RT_value), .out(multiplexer_11_out), .sel(JALR));
  assign Z = {{1{1'b0}}, and_1_out};  // Bit_Extender bit_extender_4
  Register #(.width(1)) IE_Reg (.D(1'b1), .en(LdEnInt), .Q(IE), .clk(CLK), .clr(Disable_Int));
  Multiplexer #(.width(32), .disabled(0), .enable("false")) multiplexer_12 (
    .in0(multiplexer_11_out), .in1(32'h30), .out(multiplexer_12_out), .sel(Store_PC));
  Multiplexer #(.width(32), .disabled(0), .enable("false")) multiplexer_13 (
    .in0(multiplexer_12_out), .in1(Stored_PC), .out(Next_PC), .sel(RTI));

  // Other names for the same wires on the sheet: RT[4:0] = _21b_Reg_OFFSET[4:0];
  //   Third_Reg[4:0] = _21b_Reg_OFFSET[4:0]; Second_Reg[4:0] = _21b_Reg_OFFSET[20:16]; First_Reg[4:0] = _1_Reg_RD

  // Notes on the sheet:
  //   Reg 30 =>
  //   RL <= PC+4
  //   Load from this mem address to RD
endmodule

// Registers
module Register_file (
  input  CLOCK,
  input  [4:0] Src_1_Select,
  input  Write_Enable,
  input  [4:0] Register_Write,
  input  [31:0] Write_Data,
  input  [4:0] Src_2_Select,
  output [31:0] Source_1_Data,
  output [31:0] Source_2_Data,
  output [31:0] Stored_PC
);

  wire decoder_1_out0, decoder_1_out1, decoder_1_out2, decoder_1_out3, decoder_1_out4, decoder_1_out5,
       decoder_1_out6, decoder_1_out7, decoder_1_out8, decoder_1_out9, decoder_1_out10, decoder_1_out11,
       decoder_1_out12, decoder_1_out13, decoder_1_out14, decoder_1_out15, decoder_1_out16, decoder_1_out17,
       decoder_1_out18, decoder_1_out19, decoder_1_out20, decoder_1_out21, decoder_1_out22, decoder_1_out23,
       decoder_1_out24, decoder_1_out25, decoder_1_out26, decoder_1_out27, decoder_1_out28, decoder_1_out29,
       decoder_1_out30, decoder_1_out31;
  wire [31:0] register_1_q, register_2_q, register_3_q, register_4_q, register_5_q, register_6_q,
       register_7_q, register_8_q, register_9_q, register_10_q, register_11_q, register_12_q, register_13_q,
       register_14_q, register_15_q, register_16_q, register_17_q, register_18_q, register_19_q,
       register_20_q, register_21_q, register_22_q, register_23_q, register_24_q, register_25_q,
       register_26_q, register_27_q, register_28_q, register_29_q, register_30_q, register_32_q;

  Decoder #(.select(5), .disabled(0)) decoder_1 (
    .out0(decoder_1_out0), .out1(decoder_1_out1), .out2(decoder_1_out2), .out3(decoder_1_out3),
    .out4(decoder_1_out4), .out5(decoder_1_out5), .out6(decoder_1_out6), .out7(decoder_1_out7),
    .out8(decoder_1_out8), .out9(decoder_1_out9), .out10(decoder_1_out10), .out11(decoder_1_out11),
    .out12(decoder_1_out12), .out13(decoder_1_out13), .out14(decoder_1_out14), .out15(decoder_1_out15),
    .out16(decoder_1_out16), .out17(decoder_1_out17), .out18(decoder_1_out18), .out19(decoder_1_out19),
    .out20(decoder_1_out20), .out21(decoder_1_out21), .out22(decoder_1_out22), .out23(decoder_1_out23),
    .out24(decoder_1_out24), .out25(decoder_1_out25), .out26(decoder_1_out26), .out27(decoder_1_out27),
    .out28(decoder_1_out28), .out29(decoder_1_out29), .out30(decoder_1_out30), .out31(decoder_1_out31),
    .sel(Register_Write), .en(Write_Enable));
  Register #(.width(32)) register_1 (.D({32{1'b0}}), .en(decoder_1_out0), .Q(register_1_q), .clk(CLOCK));  // open: clr
  Register #(.width(32)) register_2 (.D(Write_Data), .en(decoder_1_out1), .Q(register_2_q), .clk(CLOCK));  // open: clr
  Register #(.width(32)) register_3 (.D(Write_Data), .en(decoder_1_out2), .Q(register_3_q), .clk(CLOCK));  // open: clr
  Register #(.width(32)) register_4 (.D(Write_Data), .en(decoder_1_out3), .Q(register_4_q), .clk(CLOCK));  // open: clr
  Register #(.width(32)) register_5 (.D(Write_Data), .en(decoder_1_out4), .Q(register_5_q), .clk(CLOCK));  // open: clr
  Register #(.width(32)) register_6 (.en(decoder_1_out5), .Q(register_6_q), .clk(CLOCK));  // open: D, clr
  Register #(.width(32)) register_7 (.D(Write_Data), .en(decoder_1_out6), .Q(register_7_q), .clk(CLOCK), .clr(CLOCK));
  Register #(.width(32)) register_8 (.D(Write_Data), .en(decoder_1_out7), .Q(register_8_q), .clk(CLOCK));  // open: clr
  Register #(.width(32)) register_9 (.D(Write_Data), .en(decoder_1_out8), .Q(register_9_q), .clk(CLOCK));  // open: clr
  Register #(.width(32)) register_10 (.D(Write_Data), .en(decoder_1_out9), .Q(register_10_q), .clk(CLOCK), .clr(CLOCK));
  Register #(.width(32)) register_11 (
    .D(Write_Data), .en(decoder_1_out10), .Q(register_11_q), .clk(CLOCK), .clr(CLOCK));
  Register #(.width(32)) register_12 (
    .D(Write_Data), .en(decoder_1_out11), .Q(register_12_q), .clk(CLOCK));  // open: clr
  Register #(.width(32)) register_13 (
    .D(Write_Data), .en(decoder_1_out12), .Q(register_13_q), .clk(CLOCK));  // open: clr
  Register #(.width(32)) register_14 (
    .D(Write_Data), .en(decoder_1_out13), .Q(register_14_q), .clk(CLOCK));  // open: clr
  Register #(.width(32)) register_15 (
    .D(Write_Data), .en(decoder_1_out14), .Q(register_15_q), .clk(CLOCK));  // open: clr
  Register #(.width(32)) register_16 (
    .D(Write_Data), .en(decoder_1_out15), .Q(register_16_q), .clk(CLOCK));  // open: clr
  Register #(.width(32)) register_17 (
    .D(Write_Data), .en(decoder_1_out16), .Q(register_17_q), .clk(CLOCK));  // open: clr
  Register #(.width(32)) register_18 (
    .D(Write_Data), .en(decoder_1_out17), .Q(register_18_q), .clk(CLOCK));  // open: clr
  Register #(.width(32)) register_19 (
    .D(Write_Data), .en(decoder_1_out18), .Q(register_19_q), .clk(CLOCK));  // open: clr
  Register #(.width(32)) register_20 (
    .D(Write_Data), .en(decoder_1_out19), .Q(register_20_q), .clk(CLOCK));  // open: clr
  Register #(.width(32)) register_21 (
    .D(Write_Data), .en(decoder_1_out20), .Q(register_21_q), .clk(CLOCK));  // open: clr
  Register #(.width(32)) register_22 (
    .D(Write_Data), .en(decoder_1_out21), .Q(register_22_q), .clk(CLOCK));  // open: clr
  Register #(.width(32)) register_23 (
    .D(Write_Data), .en(decoder_1_out22), .Q(register_23_q), .clk(CLOCK));  // open: clr
  Register #(.width(32)) register_24 (
    .D(Write_Data), .en(decoder_1_out23), .Q(register_24_q), .clk(CLOCK));  // open: clr
  Register #(.width(32)) register_25 (
    .D(Write_Data), .en(decoder_1_out24), .Q(register_25_q), .clk(CLOCK), .clr(CLOCK));
  Register #(.width(32)) register_26 (
    .D(Write_Data), .en(decoder_1_out25), .Q(register_26_q), .clk(CLOCK));  // open: clr
  Register #(.width(32)) register_27 (
    .D(Write_Data), .en(decoder_1_out26), .Q(register_27_q), .clk(CLOCK));  // open: clr
  Register #(.width(32)) register_28 (
    .D(Write_Data), .en(decoder_1_out27), .Q(register_28_q), .clk(CLOCK));  // open: clr
  Register #(.width(32)) register_29 (
    .D(Write_Data), .en(decoder_1_out28), .Q(register_29_q), .clk(CLOCK));  // open: clr
  Register #(.width(32)) register_30 (
    .D(Write_Data), .en(decoder_1_out29), .Q(register_30_q), .clk(CLOCK));  // open: clr
  Register #(.width(32)) register_31 (.D(Write_Data), .en(decoder_1_out30), .Q(Stored_PC), .clk(CLOCK));  // open: clr
  Register #(.width(32)) register_32 (
    .D(Write_Data), .en(decoder_1_out31), .Q(register_32_q), .clk(CLOCK));  // open: clr
  Multiplexer #(.select(5), .width(32), .disabled(0), .enable("false")) multiplexer_1 (
    .in0(register_1_q), .in1(register_2_q), .in2(register_3_q), .in3(register_4_q), .in4(register_5_q),
    .in5(register_6_q), .in6(register_7_q), .in7(register_8_q), .in8(register_9_q), .in9(register_10_q),
    .in10(register_11_q), .in11(register_12_q), .in12(register_13_q), .in13(register_14_q),
    .in14(register_15_q), .in15(register_16_q), .in16(register_17_q), .in17(register_18_q),
    .in18(register_19_q), .in19(register_20_q), .in20(register_21_q), .in21(register_22_q),
    .in22(register_23_q), .in23(register_24_q), .in24(register_25_q), .in25(register_26_q),
    .in26(register_27_q), .in27(register_28_q), .in28(register_29_q), .in29(register_30_q), .in30(Stored_PC),
    .in31(register_32_q), .out(Source_1_Data), .sel(Src_1_Select));
  Multiplexer #(.select(5), .width(32), .disabled(0), .enable("false")) multiplexer_2 (
    .in0(register_1_q), .in1(register_2_q), .in2(register_3_q), .in3(register_4_q), .in4(register_5_q),
    .in5(register_6_q), .in6(register_7_q), .in7(register_8_q), .in8(register_9_q), .in9(register_10_q),
    .in10(register_11_q), .in11(register_12_q), .in12(register_13_q), .in13(register_14_q),
    .in14(register_15_q), .in15(register_16_q), .in16(register_17_q), .in17(register_18_q),
    .in18(register_19_q), .in19(register_20_q), .in20(register_21_q), .in21(register_22_q),
    .in22(register_23_q), .in23(register_24_q), .in24(register_25_q), .in25(register_26_q),
    .in26(register_27_q), .in27(register_28_q), .in28(register_29_q), .in29(register_30_q), .in30(Stored_PC),
    .in31(register_32_q), .out(Source_2_Data), .sel(Src_2_Select));
endmodule

// Memory
module Mem (
  input  Load_B_W,
  input  [1:0] LS_2b_of__address,
  input  Store_byte_word,
  input  [7:0] Store_Byte_0,
  input  [7:0] Store_Byte_3,
  input  Store_Enable,
  input  [7:0] Store_Byte_2,
  input  [7:0] Store_Byte_1,
  input  [23:0] _24b__address,
  output [31:0] Load_Data,
  output INT
);

  wire and_1_out, and_2_out, demultiplexer_1_out0, demultiplexer_1_out1, demultiplexer_1_out2,
       demultiplexer_1_out3, not_1_out, or_1_out, or_2_out, or_3_out, or_4_out, or_5_out;
  wire [7:0] controlled_buffer_1_out, controlled_buffer_3_out, controlled_buffer_4_out, multiplexer_1_out,
       multiplexer_4_out, multiplexer_6_out, multiplexer_8_out, ram_2_data;

  not not_1 (not_1_out, Store_Enable);
  Demultiplexer #(.select(2), .disabled(0), .enable("false")) demultiplexer_1 (
    .out0(demultiplexer_1_out0), .out1(demultiplexer_1_out1), .out2(demultiplexer_1_out2),
    .out3(demultiplexer_1_out3), .in(1'b1), .sel(LS_2b_of__address));
  Multiplexer #(.width(8), .disabled(0), .enable("false")) multiplexer_1 (
    .in0(Store_Byte_0), .in1(Store_Byte_3), .out(multiplexer_1_out), .sel(Store_byte_word));
  or or_1 (or_1_out, demultiplexer_1_out3, Store_byte_word, Load_B_W);
  Multiplexer #(.width(8), .disabled(0), .enable("false")) multiplexer_2 (
    .in0({8{1'b0}}), .in1(controlled_buffer_1_out), .out(Load_Data[31:24]), .sel(Load_B_W));
  assign controlled_buffer_1_out = Store_Enable ? multiplexer_1_out : 8'bz;  // Controlled_Buffer controlled_buffer_1
  RAM #(.addrWidth(24), .bus("asynch")) ram_1 (
    .addr(_24b__address), .data(controlled_buffer_1_out), .sel(or_1_out), .ld(not_1_out));  // open: clr
  Multiplexer #(.width(8), .disabled(0), .enable("false")) multiplexer_3 (
    .in0({8{1'b0}}), .in1(ram_2_data), .out(Load_Data[23:16]), .sel(Load_B_W));
  or or_2 (or_2_out, demultiplexer_1_out2, Store_byte_word, Load_B_W);
  Multiplexer #(.width(8), .disabled(0), .enable("false")) multiplexer_4 (
    .in0(Store_Byte_0), .in1(Store_Byte_2), .out(multiplexer_4_out), .sel(Store_byte_word));
  RAM #(.addrWidth(24), .bus("asynch")) ram_2 (
    .addr(_24b__address), .data(ram_2_data), .sel(or_2_out), .ld(not_1_out));  // open: clr
  Multiplexer #(.width(8), .disabled(0), .enable("false")) multiplexer_5 (
    .in0({8{1'b0}}), .in1(controlled_buffer_3_out), .out(Load_Data[15:8]), .sel(Load_B_W));
  assign ram_2_data = Store_Enable ? multiplexer_4_out : 8'bz;  // Controlled_Buffer controlled_buffer_2
  Multiplexer #(.width(8), .disabled(0), .enable("false")) multiplexer_6 (
    .in0(Store_Byte_0), .in1(Store_Byte_1), .out(multiplexer_6_out), .sel(Store_byte_word));
  or or_3 (or_3_out, demultiplexer_1_out1, Store_byte_word, Load_B_W);
  Multiplexer #(.width(8), .disabled(0), .enable("false")) multiplexer_7 (
    .in0(multiplexer_8_out), .in1(controlled_buffer_4_out), .out(Load_Data[7:0]), .sel(Load_B_W));
  Multiplexer #(.select(2), .width(8), .disabled(0), .enable("false")) multiplexer_8 (
    .in0(controlled_buffer_4_out), .in1(controlled_buffer_3_out), .in2(ram_2_data),
    .in3(controlled_buffer_1_out), .out(multiplexer_8_out), .sel(LS_2b_of__address));
  assign controlled_buffer_3_out = Store_Enable ? multiplexer_6_out : 8'bz;  // Controlled_Buffer controlled_buffer_3
  RAM #(.addrWidth(24), .bus("asynch")) ram_3 (
    .addr(_24b__address), .data(controlled_buffer_3_out), .sel(or_3_out), .ld(not_1_out));  // open: clr
  or or_4 (or_4_out, demultiplexer_1_out0, Store_byte_word, Load_B_W);
  or or_5 (or_5_out, LS_2b_of__address[0], LS_2b_of__address[1]);
  assign controlled_buffer_4_out = Store_Enable ? Store_Byte_0 : 8'bz;  // Controlled_Buffer controlled_buffer_4
  RAM #(.addrWidth(24), .bus("asynch")) ram_4 (
    .addr(_24b__address), .data(controlled_buffer_4_out), .sel(or_4_out), .ld(not_1_out));  // open: clr
  and and_1 (and_1_out, Load_B_W, or_5_out);
  and and_2 (and_2_out, or_5_out, Store_byte_word);
  or or_6 (INT, and_1_out, and_2_out);

  // Notes on the sheet:
  //   Byte 3
  //   Byte 2
  //   Byte 1
  //   Byte 0
endmodule

module ALU (
  input  [31:0] Src_1_Data,
  input  [31:0] Src_2__Data,
  input  [1:0] Op,
  output [31:0] ALU_out,
  output ALU_Zero
);

  wire adder_1_cout, subtractor_1_bout;
  wire [31:0] adder_1_out, nand_1_out, subtractor_1_out, xor_1_out;

  Adder #(.width(32)) adder_1 (.a(Src_1_Data), .b(Src_2__Data), .out(adder_1_out), .cin(1'b0), .cout(adder_1_cout));
  Subtractor #(.width(32)) subtractor_1 (
    .a(Src_1_Data), .b(Src_2__Data), .out(subtractor_1_out), .bin(1'b0), .bout(subtractor_1_bout));
  assign nand_1_out = ~(Src_2__Data & Src_1_Data);  // NAND_Gate nand_1, 32 bits wide
  assign xor_1_out = Src_2__Data ^ Src_1_Data;  // XOR_Gate xor_1, 32 bits wide
  Multiplexer #(.select(2), .width(32), .disabled(0), .enable("false")) multiplexer_1 (
    .in0(adder_1_out), .in1(subtractor_1_out), .in2(nand_1_out), .in3(xor_1_out), .out(ALU_out), .sel(Op));
  nor nor_1 (ALU_Zero, ALU_out[0], ALU_out[1], ALU_out[2], ALU_out[3], ALU_out[4], ALU_out[5], ALU_out[6], ALU_out[7], ALU_out[8], ALU_out[9], ALU_out[10], ALU_out[11], ALU_out[12], ALU_out[13], ALU_out[14], ALU_out[15], ALU_out[16], ALU_out[17], ALU_out[18], ALU_out[19], ALU_out[20], ALU_out[21], ALU_out[22], ALU_out[23], ALU_out[24], ALU_out[25], ALU_out[26], ALU_out[27], ALU_out[28], ALU_out[29], ALU_out[30], ALU_out[31]);
endmodule

module Control (
  input  CLK,
  input  [5:0] OPCODE,
  input  [1:0] Branch_2bit,
  input  IE,
  input  INT,
  output RTI,
  output Disable_Int,
  output Store_PC,
  output IntAck,
  output LdEnInt,
  output Branch,
  output Load,
  output PC_WE,
  output MAR_WE,
  output MDR_WE,
  output IR_WE,
  output ALUOP1,
  output ALUOP0,
  output ALUSrc1,
  output LD_ADR,
  output Mem_to_Reg,
  output Store_B_W,
  output Reg_Write_Enable,
  output Load_B_W,
  output Load_Enable,
  output Store_Enable,
  output JALR
);

  wire [0:0] and_1_out;
  wire [9:0] rom_1_data;
  wire [31:0] bit_extender_1_out, multiplexer_1_out, rom_2_data, rom_3_data, rom_4_data, State_q;

  Register #(.width(32)) State (.D(multiplexer_1_out), .en(CLK), .Q(State_q), .clk(CLK));  // open: clr
  and and_1 (and_1_out[0], IE, INT);
  ROM #(.addrWidth(24), .dataWidth(32)) rom_1 (
    .addr(State_q[23:0]),
    .data({JALR, Store_Enable, Load_Enable, Load_B_W, Reg_Write_Enable, Store_B_W, Mem_to_Reg, LD_ADR, ALUSrc1, ALUOP0, ALUOP1, IR_WE, MDR_WE, MAR_WE, PC_WE, Load, Branch, LdEnInt, IntAck, Store_PC, Disable_Int, RTI, rom_1_data}));  // open: sel
  Multiplexer #(.select(2), .width(32), .disabled(0), .enable("false")) multiplexer_1 (
    .in0(bit_extender_1_out), .in1(rom_2_data), .in2(rom_3_data), .in3(rom_4_data), .out(multiplexer_1_out),
    .sel(rom_1_data[1:0]));
  ROM #(.addrWidth(6), .dataWidth(32)) rom_2 (.addr(OPCODE), .data(rom_2_data));  // open: sel
  ROM #(.addrWidth(2), .dataWidth(32)) rom_3 (.addr(Branch_2bit), .data(rom_3_data));  // open: sel
  ROM #(.addrWidth(2), .dataWidth(32)) rom_4 (.addr({1'b0, and_1_out[0]}), .data(rom_4_data));  // open: sel
  assign bit_extender_1_out = {{19{1'b0}}, {LdEnInt, IntAck, Store_PC, Disable_Int, RTI, rom_1_data[9:2]}};  // Bit_Extender bit_extender_1

  // Notes on the sheet:
  //   contents of rom_1 (hex, n*v repeats v):
  //   30040007 30080008 3010000c 1 38000014 38020000 0 0 38400024 38420000 0 0 38200034 38220000 0 0
  //   38600044 38620000 0 0 38800054 38820000 0 0 39800064 39820000 0 0 32850074 3a820000 0 0 22850084
  //   2a820000 0 0 4850094 44830000 0 0 8500a4 40820000 0 0 300080b4 30028000 0 0 b10000c4 b9020000 0 0
  //   320100d4 3a030000 0 0 24000 0 0 0 20800 0 0 0 24400 15*0 8023804
  //   contents of rom_2 (hex, n*v repeats v):
  //   4 8 c 10 14 18 1c 20 24 28 2c 30 34 38 3c 40
  //   contents of rom_4 (hex, n*v repeats v):
  //   1 50
  //   <= 0x50 in main ROM
  //   Dispatch
  //   Branch?
  //   State(9 bits)
endmodule
