// Logisim project Proj3_faster (1).circ as structural Verilog: 5 circuits, main circuit Pipeline
module Pipeline (
);

  wire alu_2_alu_zero, and_1_out, and_6_out, Branch_RR, CLK, clock_1_out, comparator_1_eq, comparator_2_eq,
       comparator_3_eq, comparator_4_eq, d_ff_1_q, Flush, JALR, JALR_RR, LW, nand_1_out, nand_2_out,
       nand_3_out, nor_2_out, not_1_out, not_2_out, not_3_out, not_4_out, not_5_out, not_6_out, not_7_out,
       not_8_out, not_9_out, not_10_out, not_11_out, not_12_out, or_1_out, or_3_out, or_4_out, RAW_RS1,
       RAW_RS1_2, RAW_RS2, RAW_RS2_2, Store_RR;
  wire [3:0] EX_Mem_RD_q, Ex_Mem_RS1_q, Ex_Mem_RS2_q, ID_EX_RD_q, ID_EX_RS1_q, ID_EX_RS2_q,
       IF_ID_First_Reg_q, IF_ID_Second_Reg_q, IF_ID_Third_Reg_q, Mem_WB_RD_q, multiplexer_1_out,
       multiplexer_2_out, multiplexer_4_out, multiplexer_8_out, multiplexer_9_out;
  wire [7:0] EX_Mem_OP_q, ID_EX_OP_q, IF_ID_OP_q, Mem_WB_OP_q;
  wire [15:0] IF_ID_Immediate_q;
  wire [31:0] alu_3_alu_out, ALU_Res, ALU_Res_2, EX_Mem_Store_Value_q, Extended_OFF, Extended_Off_RR,
       ID_EX_PC_1_q, ID_EX_Src1_q, ID_EX_Src2_q, IF_ID_PC_1_2_q, IF_ID_PC_1_q, instr_mem_1_instr_out,
       Instr_Reg_q, Mem_out, Mem_WB_ALU_Res_q, Mem_WB_Mem_Out_q, multiplexer_5_out, multiplexer_6_out,
       multiplexer_7_out, multiplexer_11_out, multiplexer_12_out, multiplexer_13_out, multiplexer_14_out,
       multiplexer_15_out, multiplexer_16_out, Next_PC, PC_1, PC_q, reg_file_1_source_1_data,
       reg_file_1_source_2_data, RT;

  ALU alu_1 (.Src_1_Data(PC_q), .Src_2__Data(32'h1), .Op(2'b00), .ALU_out(PC_1));  // open: ALU_Zero
  Register #(.width(32)) PC (.D(Next_PC), .en(CLK), .Q(PC_q), .clk(CLK));  // open: clr
  Instr_Mem instr_mem_1 (._24b_Address(PC_q[23:0]), .Instr_Out(instr_mem_1_instr_out));
  not not_1 (not_1_out, CLK);
  Register #(.width(32)) Instr_Reg (.D(instr_mem_1_instr_out), .en(CLK), .Q(Instr_Reg_q), .clk(CLK), .clr(d_ff_1_q));
  D_Flip_Flop d_ff_1 (.clk(not_1_out), .D(Flush), .Q(d_ff_1_q));  // open: Qn, preset, en, reset
  Register #(.width(32)) IF_ID_PC_1 (.D(PC_1), .en(CLK), .Q(IF_ID_PC_1_q), .clk(CLK));  // open: clr
  Register #(.width(32)) IF_ID_PC_1_2 (.D(IF_ID_PC_1_q), .en(CLK), .Q(IF_ID_PC_1_2_q), .clk(CLK));  // open: clr
  Register IF_ID_OP (
    .D(Instr_Reg_q[31:24]), .en(CLK), .Q({IF_ID_OP_q[7:6], Store_RR, Branch_RR, JALR_RR, IF_ID_OP_q[2:0]}),
    .clk(CLK));  // open: clr
  Register #(.width(4)) IF_ID_First_Reg (
    .D(Instr_Reg_q[23:20]), .en(CLK), .Q(IF_ID_First_Reg_q), .clk(CLK));  // open: clr
  Register #(.width(4)) IF_ID_Second_Reg (
    .D(Instr_Reg_q[19:16]), .en(CLK), .Q(IF_ID_Second_Reg_q), .clk(CLK));  // open: clr
  Register #(.width(16)) IF_ID_Immediate (
    .D(Instr_Reg_q[15:0]), .en(CLK), .Q(IF_ID_Immediate_q), .clk(CLK));  // open: clr
  Register #(.width(4)) IF_ID_Third_Reg (
    .D(Instr_Reg_q[15:12]), .en(CLK), .Q(IF_ID_Third_Reg_q), .clk(CLK));  // open: clr
  or or_1 (or_1_out, IF_ID_OP_q[6], Store_RR);
  Multiplexer #(.width(4), .disabled(0), .enable("false")) multiplexer_1 (
    .in0(IF_ID_Second_Reg_q), .in1(IF_ID_First_Reg_q), .out(multiplexer_1_out), .sel(IF_ID_OP_q[2]));
  Multiplexer #(.width(4), .disabled(0), .enable("false")) multiplexer_2 (
    .in0(IF_ID_Third_Reg_q), .in1(IF_ID_Second_Reg_q), .out(multiplexer_2_out), .sel(or_1_out));
  Multiplexer #(.width(32), .disabled(0), .enable("false")) multiplexer_3 (
    .in0(multiplexer_5_out), .in1(RT), .out(Next_PC), .sel(JALR_RR));
  or or_2 (Flush, JALR_RR, and_1_out);
  Reg_File reg_file_1 (
    .CLOCK(CLK), .Src_1_Select(multiplexer_1_out), .Write_Enable(nor_2_out), .Register_Write(Mem_WB_RD_q),
    .Write_Data(multiplexer_16_out), .Src_2_Select(multiplexer_2_out),
    .Source_1_Data(reg_file_1_source_1_data), .Source_2_Data(reg_file_1_source_2_data));
  Multiplexer #(.width(4), .disabled(0), .enable("false")) multiplexer_4 (
    .in0(IF_ID_First_Reg_q), .in1(IF_ID_Second_Reg_q), .out(multiplexer_4_out), .sel(JALR_RR));
  or or_3 (or_3_out, JALR_RR, Branch_RR, Store_RR);
  Multiplexer #(.width(32), .disabled(0), .enable("false")) multiplexer_5 (
    .in0(PC_1), .in1(alu_3_alu_out), .out(multiplexer_5_out), .sel(and_1_out));
  and and_1 (and_1_out, Branch_RR, alu_2_alu_zero);
  ALU alu_2 (
    .Src_1_Data(multiplexer_11_out), .Src_2__Data(RT), .Op(2'b01), .ALU_Zero(alu_2_alu_zero));  // open: ALU_out
  Multiplexer #(.width(32), .disabled(0), .enable("false")) multiplexer_6 (
    .in0(reg_file_1_source_1_data), .in1(ALU_Res), .out(multiplexer_6_out), .sel(RAW_RS1));
  Multiplexer #(.width(32), .disabled(0), .enable("false")) multiplexer_7 (
    .in0(reg_file_1_source_2_data), .in1(ALU_Res), .out(multiplexer_7_out), .sel(RAW_RS2));
  assign Extended_Off_RR = {{16{IF_ID_Immediate_q[15]}}, IF_ID_Immediate_q};  // Bit_Extender bit_extender_1
  Multiplexer #(.width(4), .disabled(0), .enable("false")) multiplexer_8 (
    .in0(IF_ID_Third_Reg_q), .in1(IF_ID_Second_Reg_q), .out(multiplexer_8_out), .sel(or_4_out));
  or or_4 (or_4_out, JALR_RR, Branch_RR, Store_RR);
  Multiplexer #(.width(4), .disabled(0), .enable("false")) multiplexer_9 (
    .in0(IF_ID_Second_Reg_q), .in1(IF_ID_First_Reg_q), .out(multiplexer_9_out), .sel(or_3_out));
  Multiplexer #(.select(2), .width(32), .disabled(0), .enable("false")) multiplexer_10 (
    .in0(multiplexer_6_out), .in1(multiplexer_6_out), .in2(ALU_Res_2), .in3(Mem_out), .out(RT),
    .sel({RAW_RS1_2, LW}));
  Multiplexer #(.select(2), .width(32), .disabled(0), .enable("false")) multiplexer_11 (
    .in0(multiplexer_7_out), .in1(multiplexer_7_out), .in2(ALU_Res_2), .in3(Mem_out),
    .out(multiplexer_11_out), .sel({RAW_RS2_2, LW}));
  ALU alu_3 (
    .Src_1_Data(Extended_Off_RR), .Src_2__Data(IF_ID_PC_1_2_q), .Op(2'b00), .ALU_out(alu_3_alu_out));  // open: ALU_Zero
  Register ID_EX_OP (
    .D({IF_ID_OP_q[7:6], Store_RR, Branch_RR, JALR_RR, IF_ID_OP_q[2:0]}), .en(CLK),
    .Q({ID_EX_OP_q[7:4], JALR, ID_EX_OP_q[2:0]}), .clk(CLK));  // open: clr
  Register #(.width(32)) ID_EX_PC_1 (.D(IF_ID_PC_1_2_q), .en(CLK), .Q(ID_EX_PC_1_q), .clk(CLK));  // open: clr
  Register #(.width(32)) ID_EX_Src1 (.D(RT), .en(CLK), .Q(ID_EX_Src1_q), .clk(CLK));  // open: clr
  Register #(.width(32)) ID_EX_Src2 (.D(multiplexer_11_out), .en(CLK), .Q(ID_EX_Src2_q), .clk(CLK));  // open: clr
  Register #(.width(32)) ID_EX_Extended_OFF (.D(Extended_Off_RR), .en(CLK), .Q(Extended_OFF), .clk(CLK));  // open: clr
  Register #(.width(4)) ID_EX_RS1 (.D(IF_ID_Second_Reg_q), .en(CLK), .Q(ID_EX_RS1_q), .clk(CLK));  // open: clr
  Register #(.width(4)) ID_EX_RS2 (.D(IF_ID_Third_Reg_q), .en(CLK), .Q(ID_EX_RS2_q), .clk(CLK));  // open: clr
  Register #(.width(4)) ID_EX_RD (.D(multiplexer_4_out), .en(CLK), .Q(ID_EX_RD_q), .clk(CLK));  // open: clr
  not not_2 (not_2_out, multiplexer_9_out[2]);
  not not_3 (not_3_out, multiplexer_9_out[3]);
  Multiplexer #(.width(32), .disabled(0), .enable("false")) multiplexer_12 (
    .in0(ID_EX_Src1_q), .in1(ID_EX_PC_1_q), .out(multiplexer_12_out), .sel(ID_EX_OP_q[1]));
  Multiplexer #(.width(32), .disabled(0), .enable("false")) multiplexer_13 (
    .in0(ID_EX_Src2_q), .in1(Extended_OFF), .out(multiplexer_13_out), .sel(ID_EX_OP_q[0]));
  not not_4 (not_4_out, multiplexer_8_out[0]);
  not not_5 (not_5_out, multiplexer_8_out[1]);
  not not_6 (not_6_out, multiplexer_8_out[2]);
  not not_7 (not_7_out, multiplexer_8_out[3]);
  Comparator #(.width(4), .mode("unsigned")) comparator_1 (
    .a(multiplexer_8_out), .b(ID_EX_RD_q), .eq(comparator_1_eq));  // open: gt, lt
  Comparator #(.width(4), .mode("unsigned")) comparator_2 (
    .a(multiplexer_9_out), .b(ID_EX_RD_q), .eq(comparator_2_eq));  // open: gt, lt
  not not_8 (not_8_out, multiplexer_9_out[0]);
  not not_9 (not_9_out, multiplexer_9_out[1]);
  nand nand_1 (nand_1_out, not_8_out, not_9_out, not_2_out, not_3_out);
  Multiplexer #(.width(32), .disabled(0), .enable("false")) multiplexer_14 (
    .in0(multiplexer_12_out), .in1(Extended_OFF), .out(multiplexer_14_out), .sel(ID_EX_OP_q[5]));
  Multiplexer #(.width(32), .disabled(0), .enable("false")) multiplexer_15 (
    .in0(multiplexer_13_out), .in1(Extended_OFF), .out(multiplexer_15_out), .sel(JALR));
  nand nand_2 (nand_2_out, not_4_out, not_5_out, not_6_out, not_7_out);
  and and_2 (RAW_RS1, comparator_2_eq, nand_1_out);
  ALU alu_4 (
    .Src_1_Data(multiplexer_14_out), .Src_2__Data(multiplexer_15_out), .Op(ID_EX_OP_q[7:6]), .ALU_out(ALU_Res));  // open: ALU_Zero
  and and_3 (RAW_RS2, nand_2_out, comparator_1_eq);
  Register EX_Mem_OP (.D({ID_EX_OP_q[7:4], JALR, ID_EX_OP_q[2:0]}), .en(CLK), .Q(EX_Mem_OP_q), .clk(CLK));  // open: clr
  Register #(.width(32)) EX_Mem_Store_Value (
    .D(multiplexer_12_out), .en(CLK), .Q(EX_Mem_Store_Value_q), .clk(CLK));  // open: clr
  Register #(.width(32)) EX_Mem_ALU_Res (.D(ALU_Res), .en(CLK), .Q(ALU_Res_2), .clk(CLK));  // open: clr
  Register #(.width(4)) Ex_Mem_RS1 (.D(ID_EX_RS1_q), .en(CLK), .Q(Ex_Mem_RS1_q), .clk(CLK));  // open: clr
  Register #(.width(4)) Ex_Mem_RS2 (.D(ID_EX_RS2_q), .en(CLK), .Q(Ex_Mem_RS2_q), .clk(CLK));  // open: clr
  Register #(.width(4)) EX_Mem_RD (.D(ID_EX_RD_q), .en(CLK), .Q(EX_Mem_RD_q), .clk(CLK));  // open: clr
  not not_10 (not_10_out, EX_Mem_OP_q[0]);
  not not_11 (not_11_out, EX_Mem_OP_q[6]);
  not not_12 (not_12_out, EX_Mem_OP_q[7]);
  Mem mem_1 (
    .Data_to_store(EX_Mem_Store_Value_q), ._24b_WordAddress(ALU_Res_2[23:0]), .Store(EX_Mem_OP_q[5]),
    .Data_Out(Mem_out));
  Comparator #(.width(4), .mode("unsigned")) comparator_3 (
    .a(EX_Mem_RD_q), .b(multiplexer_8_out), .eq(comparator_3_eq));  // open: gt, lt
  Comparator #(.width(4), .mode("unsigned")) comparator_4 (
    .a(EX_Mem_RD_q), .b(multiplexer_9_out), .eq(comparator_4_eq));  // open: gt, lt
  nor nor_1 (LW, not_10_out, EX_Mem_OP_q[1], EX_Mem_OP_q[2], EX_Mem_OP_q[3], EX_Mem_OP_q[4], EX_Mem_OP_q[5], not_11_out, not_12_out);
  and and_4 (RAW_RS2_2, comparator_3_eq, nand_2_out);
  and and_5 (RAW_RS1_2, comparator_4_eq, nand_1_out);
  Register Mem_WB_OP (.D(EX_Mem_OP_q), .en(CLK), .Q(Mem_WB_OP_q), .clk(CLK));  // open: clr
  Register #(.width(32)) Mem_WB_Mem_Out (.D(Mem_out), .en(CLK), .Q(Mem_WB_Mem_Out_q), .clk(CLK));  // open: clr
  Register #(.width(32)) Mem_WB_ALU_Res (.D(ALU_Res_2), .en(CLK), .Q(Mem_WB_ALU_Res_q), .clk(CLK));  // open: clr
  Register #(.width(4)) Ex_Mem_RS1_2 (.D(Ex_Mem_RS1_q), .en(CLK), .clk(CLK));  // open: Q, clr
  Register #(.width(4)) Ex_Mem_RS2_2 (.D(Ex_Mem_RS2_q), .en(CLK), .clk(CLK));  // open: Q, clr
  Register #(.width(4)) Mem_WB_RD (.D(EX_Mem_RD_q), .en(CLK), .Q(Mem_WB_RD_q), .clk(CLK));  // open: clr
  Clock clock_1 (.out(clock_1_out));
  and and_6 (and_6_out, Mem_WB_OP_q[6], Mem_WB_OP_q[7]);
  Multiplexer #(.width(32), .disabled(0), .enable("false")) multiplexer_16 (
    .in0(Mem_WB_ALU_Res_q), .in1(Mem_WB_Mem_Out_q), .out(multiplexer_16_out), .sel(and_6_out));
  nor nor_2 (nor_2_out, Mem_WB_OP_q[5], Mem_WB_OP_q[4]);
  assign CLK = nand_3_out ? clock_1_out : 1'bz;  // Controlled_Buffer controlled_buffer_1
  nand nand_3 (nand_3_out, Mem_WB_OP_q[0], Mem_WB_OP_q[1], Mem_WB_OP_q[2], Mem_WB_OP_q[3], Mem_WB_OP_q[4], Mem_WB_OP_q[5], Mem_WB_OP_q[6], Mem_WB_OP_q[7]);
  Counter #(.width(32), .max('hffffffff)) counter_1 (.count(CLK), .clk(CLK));  // open: load, D, Q, carry, clr

  // Notes on the sheet:
  //   Reg write unless store or branch
endmodule

module Reg_File (
  input  CLOCK,
  input  [3:0] Src_1_Select,
  input  Write_Enable,
  input  [3:0] Register_Write,
  input  [31:0] Write_Data,
  input  [3:0] Src_2_Select,
  output [31:0] Source_1_Data,
  output [31:0] Source_2_Data
);

  wire decoder_1_out0, decoder_1_out1, decoder_1_out2, decoder_1_out3, decoder_1_out4, decoder_1_out5,
       decoder_1_out6, decoder_1_out7, decoder_1_out8, decoder_1_out9, decoder_1_out10, decoder_1_out11,
       decoder_1_out12, decoder_1_out13, decoder_1_out14, decoder_1_out15;
  wire [31:0] register_1_q, register_2_q, register_3_q, register_4_q, register_5_q, register_6_q,
       register_7_q, register_8_q, register_9_q, register_10_q, register_11_q, register_12_q, register_13_q,
       register_14_q, register_15_q, register_16_q;

  Decoder #(.select(4), .disabled(0)) decoder_1 (
    .out0(decoder_1_out0), .out1(decoder_1_out1), .out2(decoder_1_out2), .out3(decoder_1_out3),
    .out4(decoder_1_out4), .out5(decoder_1_out5), .out6(decoder_1_out6), .out7(decoder_1_out7),
    .out8(decoder_1_out8), .out9(decoder_1_out9), .out10(decoder_1_out10), .out11(decoder_1_out11),
    .out12(decoder_1_out12), .out13(decoder_1_out13), .out14(decoder_1_out14), .out15(decoder_1_out15),
    .sel(Register_Write), .en(Write_Enable));
  Register #(.width(32)) register_1 (.D({32{1'b0}}), .en(decoder_1_out0), .Q(register_1_q), .clk(CLOCK));  // open: clr
  Register #(.width(32)) register_2 (.D(Write_Data), .en(decoder_1_out1), .Q(register_2_q), .clk(CLOCK));  // open: clr
  Register #(.width(32)) register_3 (.D(Write_Data), .en(decoder_1_out2), .Q(register_3_q), .clk(CLOCK));  // open: clr
  Register #(.width(32)) register_4 (.D(Write_Data), .en(decoder_1_out3), .Q(register_4_q), .clk(CLOCK));  // open: clr
  Register #(.width(32)) register_5 (.D(Write_Data), .en(decoder_1_out4), .Q(register_5_q), .clk(CLOCK));  // open: clr
  Register #(.width(32)) register_6 (.D(Write_Data), .en(decoder_1_out5), .Q(register_6_q), .clk(CLOCK));  // open: clr
  Register #(.width(32)) register_7 (.D(Write_Data), .en(decoder_1_out6), .Q(register_7_q), .clk(CLOCK));  // open: clr
  Register #(.width(32)) register_8 (.D(Write_Data), .en(decoder_1_out7), .Q(register_8_q), .clk(CLOCK));  // open: clr
  Register #(.width(32)) register_9 (.D(Write_Data), .en(decoder_1_out8), .Q(register_9_q), .clk(CLOCK));  // open: clr
  Register #(.width(32)) register_10 (
    .D(Write_Data), .en(decoder_1_out9), .Q(register_10_q), .clk(CLOCK));  // open: clr
  Register #(.width(32)) register_11 (
    .D(Write_Data), .en(decoder_1_out10), .Q(register_11_q), .clk(CLOCK));  // open: clr
  Register #(.width(32)) register_12 (
    .D(Write_Data), .en(decoder_1_out11), .Q(register_12_q), .clk(CLOCK));  // open: clr
  Register #(.width(32)) register_13 (
    .D(Write_Data), .en(decoder_1_out12), .Q(register_13_q), .clk(CLOCK));  // open: clr
  Register #(.width(32)) register_14 (
    .D(Write_Data), .en(decoder_1_out13), .Q(register_14_q), .clk(CLOCK));  // open: clr
  Register #(.width(32)) register_15 (
    .D(Write_Data), .en(decoder_1_out14), .Q(register_15_q), .clk(CLOCK));  // open: clr
  Register #(.width(32)) register_16 (
    .D(Write_Data), .en(decoder_1_out15), .Q(register_16_q), .clk(CLOCK));  // open: clr
  Multiplexer #(.select(4), .width(32), .disabled(0), .enable("false")) multiplexer_1 (
    .in0(register_1_q), .in1(register_2_q), .in2(register_3_q), .in3(register_4_q), .in4(register_5_q),
    .in5(register_6_q), .in6(register_7_q), .in7(register_8_q), .in8(register_9_q), .in9(register_10_q),
    .in10(register_11_q), .in11(register_12_q), .in12(register_13_q), .in13(register_14_q),
    .in14(register_15_q), .in15(register_16_q), .out(Source_1_Data), .sel(Src_1_Select));
  Multiplexer #(.select(4), .width(32), .disabled(0), .enable("false")) multiplexer_2 (
    .in0(register_1_q), .in1(register_2_q), .in2(register_3_q), .in3(register_4_q), .in4(register_5_q),
    .in5(register_6_q), .in6(register_7_q), .in7(register_8_q), .in8(register_9_q), .in9(register_10_q),
    .in10(register_11_q), .in11(register_12_q), .in12(register_13_q), .in13(register_14_q),
    .in14(register_15_q), .in15(register_16_q), .out(Source_2_Data), .sel(Src_2_Select));
endmodule

module ALU (
  input  [31:0] Src_1_Data,
  input  [31:0] Src_2__Data,
  input  [1:0] Op,
  output [31:0] ALU_out,
  output ALU_Zero
);

  wire [31:0] adder_1_out, nand_1_out, subtractor_1_out;

  Adder #(.width(32)) adder_1 (.a(Src_1_Data), .b(Src_2__Data), .out(adder_1_out), .cin(1'b0));  // open: cout
  Subtractor #(.width(32)) subtractor_1 (
    .a(Src_1_Data), .b(Src_2__Data), .out(subtractor_1_out), .bin(1'b0));  // open: bout
  assign nand_1_out = ~(Src_2__Data & Src_1_Data);  // NAND_Gate nand_1, 32 bits wide
  Multiplexer #(.select(2), .width(32), .disabled(0), .enable("false")) multiplexer_1 (
    .in0(adder_1_out), .in1(subtractor_1_out), .in2(nand_1_out), .in3(adder_1_out), .out(ALU_out), .sel(Op));
  nor nor_1 (ALU_Zero, ALU_out[0], ALU_out[1], ALU_out[2], ALU_out[3], ALU_out[4], ALU_out[5], ALU_out[6], ALU_out[7], ALU_out[8], ALU_out[9], ALU_out[10], ALU_out[11], ALU_out[12], ALU_out[13], ALU_out[14], ALU_out[15], ALU_out[16], ALU_out[17], ALU_out[18], ALU_out[19], ALU_out[20], ALU_out[21], ALU_out[22], ALU_out[23], ALU_out[24], ALU_out[25], ALU_out[26], ALU_out[27], ALU_out[28], ALU_out[29], ALU_out[30], ALU_out[31]);
endmodule

module Mem (
  input  [31:0] Data_to_store,
  input  [23:0] _24b_WordAddress,
  input  Store,
  output [31:0] Data_Out
);

  wire not_1_out, not_2_out;
  wire [31:0] controlled_buffer_1_out;

  not not_1 (not_1_out, Store);
  assign controlled_buffer_1_out = Store ? Data_to_store : 32'bz;  // Controlled_Buffer controlled_buffer_1
  RAM #(.addrWidth(24), .dataWidth(32), .bus("asynch")) ram_1 (
    .addr(_24b_WordAddress), .data(controlled_buffer_1_out), .ld(not_1_out));  // open: sel, clr
  assign Data_Out = not_2_out ? controlled_buffer_1_out : 32'bz;  // Controlled_Buffer controlled_buffer_2
  not not_2 (not_2_out, Store);
endmodule

// IM
module Instr_Mem (
  input  [23:0] _24b_Address,
  output [31:0] Instr_Out
);

  ROM #(.addrWidth(24), .dataWidth(32)) rom_1 (.addr(_24b_Address), .data(Instr_Out));  // open: sel

  // Notes on the sheet:
  //   contents of rom_1 (hex, n*v repeats v):
  //   3e00029 c1ee0000 3100008 c1110000 3200007 c1220000 3300007 e3f0000 3100004 24a10000 ff000000 2 10 0
  //   1ee0002 24feffff 241efffe 5402000b 5401000d 122ffff 130000e e3f0000 1a0000 c12efffe 1300023 e3f0000
  //   c1feffff 1eefffe ef00000 1a00001 1eefffe ef00000 a00000 1eefffe ef00000 a00000 aa1000 80400000
  //   224000 54200001 5400fffb ef00000 a0000
endmodule
